// Logisim project Lab-11.circ as structural Verilog: 3 circuits, main circuit main
module main (
  input  D0,
  input  D1,
  input  D2,
  input  D3,
  input  [7:0] in_5,
  input  in_6,
  input  in_7,
  input  [3:0] in_8,
  input  L,
  input  [3:0] in_10,
  input  L___0_R___1,
  input  in_12,
  input  in_13,
  output Q0,
  output Q1,
  output Q2,
  output Q3,
  output [7:0] out_18,
  output Q0_2,
  output Q1_2,
  output Q2_2,
  output Q3_2,
  output [3:0] out_23,
  output [3:0] Right,
  output [3:0] Left
);

  wire C_out, clock_1_out, clock_2_out, clock_3_out, clock_4_out, not_1_out, not_2_out, not_3_out, not_4_out,
       not_5_out, not_6_out, not_7_out, or_1_out, parallel_1_out_5, parallel_2_out_5, parallel_3_out_5,
       parallel_4_out_5, r_l_1_out_5, r_l_2_out_5, r_l_3_out_5, r_l_4_out_5;

  Clock clock_1 (.out(clock_1_out));
  Clock clock_2 (.out(clock_2_out));
  not not_1 (not_1_out, L);
  Clock C (.out(C_out));
  D_Flip_Flop d_ff_1 (.clk(clock_1_out), .D(D0), .Q(Q0));  // open: Qn, preset, en, reset
  D_Flip_Flop d_ff_2 (.clk(clock_1_out), .D(D1), .Q(Q1));  // open: Qn, preset, en, reset
  D_Flip_Flop d_ff_3 (.clk(clock_1_out), .D(D2), .Q(Q2));  // open: Qn, preset, en, reset
  D_Flip_Flop d_ff_4 (.clk(clock_1_out), .D(D3), .Q(Q3));  // open: Qn, preset, en, reset
  Clock clock_3 (.out(clock_3_out));
  Parallel parallel_1 (.Qin(out_23[0]), .nLoad(not_1_out), .D(in_10[0]), .Load(L), .out_5(parallel_1_out_5));
  Parallel parallel_2 (.Qin(out_23[1]), .nLoad(not_1_out), .D(in_10[1]), .Load(L), .out_5(parallel_2_out_5));
  Parallel parallel_3 (.Qin(out_23[2]), .nLoad(not_1_out), .D(in_10[2]), .Load(L), .out_5(parallel_3_out_5));
  Parallel parallel_4 (.Qin(out_23[3]), .nLoad(not_1_out), .D(in_10[3]), .Load(L), .out_5(parallel_4_out_5));
  Register register_1 (.D(in_5), .Q(out_18), .clk(clock_3_out), .clr(in_6));  // open: en
  not not_2 (not_2_out, in_7);
  D_Flip_Flop d_ff_5 (.clk(or_1_out), .D(in_8[0]), .Q(Q0_2));  // open: Qn, preset, en, reset
  D_Flip_Flop d_ff_6 (.clk(or_1_out), .D(in_8[1]), .Q(Q1_2));  // open: Qn, preset, en, reset
  D_Flip_Flop d_ff_7 (.clk(or_1_out), .D(in_8[2]), .Q(Q2_2));  // open: Qn, preset, en, reset
  D_Flip_Flop d_ff_8 (.clk(or_1_out), .D(in_8[3]), .Q(Q3_2));  // open: Qn, preset, en, reset
  D_Flip_Flop d_ff_9 (.clk(C_out), .D(parallel_1_out_5), .Q(out_23[0]));  // open: Qn, preset, en, reset
  D_Flip_Flop d_ff_10 (.clk(C_out), .D(parallel_2_out_5), .Q(out_23[1]));  // open: Qn, preset, en, reset
  D_Flip_Flop d_ff_11 (.clk(C_out), .D(parallel_3_out_5), .Q(out_23[2]));  // open: Qn, preset, en, reset
  D_Flip_Flop d_ff_12 (.clk(C_out), .D(parallel_4_out_5), .Q(out_23[3]));  // open: Qn, preset, en, reset
  or or_1 (or_1_out, clock_2_out, not_2_out);
  Clock clock_4 (.out(clock_4_out));
  not not_3 (not_3_out, r_l_2_out_5);
  J_K_Flip_Flop j_k_ff_1 (
    .J(r_l_2_out_5), .clk(clock_4_out), .K(not_3_out), .Q(Left[3]));  // open: Qn, preset, en, reset
  not not_4 (not_4_out, r_l_1_out_5);
  J_K_Flip_Flop j_k_ff_2 (
    .J(r_l_1_out_5), .clk(clock_4_out), .K(not_4_out), .Q(Left[2]));  // open: Qn, preset, en, reset
  not not_5 (not_5_out, r_l_3_out_5);
  J_K_Flip_Flop j_k_ff_3 (
    .J(r_l_3_out_5), .clk(clock_4_out), .K(not_5_out), .Q(Left[1]));  // open: Qn, preset, en, reset
  R_L r_l_1 (.L(Left[1]), .nR(not_7_out), .L_2(L___0_R___1), .R(Left[1]), .out_5(r_l_1_out_5));
  R_L r_l_2 (.L(in_12), .nR(not_7_out), .L_2(L___0_R___1), .R(Left[2]), .out_5(r_l_2_out_5));
  J_K_Flip_Flop j_k_ff_4 (
    .J(r_l_4_out_5), .clk(clock_4_out), .K(not_6_out), .Q(Left[0]));  // open: Qn, preset, en, reset
  not not_6 (not_6_out, r_l_4_out_5);
  R_L r_l_3 (.L(Left[2]), .nR(not_7_out), .L_2(L___0_R___1), .R(Left[1]), .out_5(r_l_3_out_5));
  not not_7 (not_7_out, L___0_R___1);
  R_L r_l_4 (.L(Left[3]), .nR(not_7_out), .L_2(L___0_R___1), .R(in_13), .out_5(r_l_4_out_5));

  assign Right = {Left[0], Left[1], Left[2], Left[3]};
endmodule

module Parallel (
  input  Qin,
  input  nLoad,
  input  D,
  input  Load,
  output out_5
);

  wire and_1_out, and_2_out;

  and and_1 (and_1_out, Qin, nLoad);
  and and_2 (and_2_out, D, Load);
  or or_1 (out_5, and_1_out, and_2_out);
endmodule

module R_L (
  input  L,
  input  nR,
  input  L_2,
  input  R,
  output out_5
);

  wire and_1_out, and_2_out;

  and and_1 (and_1_out, L, nR);
  or or_1 (out_5, and_1_out, and_2_out);
  and and_2 (and_2_out, L_2, R);
endmodule
